# Fritzing sketch Diagram (saved by Fritzing 0.9.2b)
breadboards: 1

parts:
  Raspberry_Pi1 = Raspberry Pi 2
  S1 = Pushbutton [package="[THT]"]
  S2 = Pushbutton [package="[THT]"]
  S3 = Pushbutton [package="[THT]"]
  LED1 = LED - 5mm [color="Red (633nm)" package="5 mm [THT]"]
  LED2 = LED - 5mm [color="Yellow (595nm)" package="5 mm [THT]"]
  LED3 = LED - 5mm [color="Green (565nm)" package="5 mm [THT]"]
  R1 = Resistor [tolerance=±5% resistance=330 package=THT]
  R2 = Resistor [tolerance=±5% resistance=330 package=THT]
  R3 = Resistor [tolerance=±5% resistance=330 package=THT]

nets:
  N1: Raspberry_Pi1.GPIO2, S1.Pin_1, S1.Pin_2
  N2: Raspberry_Pi1.GPIO3, S2.Pin_1, S2.Pin_2
  N3: Raspberry_Pi1.GPIO4, S3.Pin_1, S3.Pin_2
  N4: Raspberry_Pi1.GPIO5, R3.Pin_0
  N5: Raspberry_Pi1.GPIO6, R2.Pin_0
  N6: Raspberry_Pi1.GPIO13, R1.Pin_0
  N7: Raspberry_Pi1.GND, S1.Pin_3, S1.Pin_4, S2.Pin_3, S2.Pin_4, S3.Pin_3, S3.Pin_4, LED1.cathode, LED2.cathode, LED3.cathode
  N8: LED1.anode, R3.Pin_1
  N9: LED2.anode, R2.Pin_1
  N10: LED3.anode, R1.Pin_1
